// Digital circuit D_reset.dig as structural Verilog
module D_reset (
  input  CLK,
  input  D,
  input  RST,
  output Q,
  output Q_2
);

  wire multiplexer_1_out, not_1_out;

  not not_1 (not_1_out, RST);
  Multiplexer multiplexer_1 (.sel(RST), .in_0(D), .in_1(not_1_out), .out(multiplexer_1_out));
  D_FF d_ff_1 (.D(multiplexer_1_out), .C(CLK), .Q(Q), .nQ(Q_2));
endmodule
