// Digital circuit counter_6.dig as structural Verilog
module counter_6 (
  input  UP,
  input  DOWN,
  input  CLK,
  output [3:0] CNT
);

  wire and_1_out, and_2_out, and_3_out, and_4_out, and_5_out, d_ff_1_q, d_ff_2_q, d_ff_3_nq, d_ff_4_nq,
       d_ff_5_nq, d_ff_6_nq, d_ff_7_nq, d_ff_8_nq, decoder_1_out_0, decoder_1_out_15, multiplexer_1_out,
       multiplexer_2_out, multiplexer_3_out, multiplexer_4_out, multiplexer_5_out, multiplexer_6_out,
       multiplexer_7_out, multiplexer_8_out, multiplexer_9_out, multiplexer_10_out, multiplexer_11_out,
       xor_1_out;
  wire [1:0] decoder_1_out_6;

  D_FF d_ff_1 (.D(DOWN), .C(CLK), .Q(d_ff_1_q));  // open: nQ
  D_FF d_ff_2 (.D(UP), .C(CLK), .Q(d_ff_2_q));  // open: nQ
  and and_1 (and_1_out, d_ff_1_q, d_ff_3_nq);
  D_FF d_ff_3 (.D(d_ff_1_q), .C(CLK), .nQ(d_ff_3_nq));  // open: Q
  and and_2 (and_2_out, d_ff_4_nq, d_ff_2_q);
  D_FF d_ff_4 (.D(d_ff_2_q), .C(CLK), .nQ(d_ff_4_nq));  // open: Q
  xor xor_1 (xor_1_out, and_2_out, and_1_out);
  and and_3 (and_3_out, multiplexer_9_out, xor_1_out);
  and and_4 (and_4_out, multiplexer_10_out, and_3_out);
  and and_5 (and_5_out, multiplexer_11_out, and_4_out);
  Multiplexer multiplexer_1 (.sel(xor_1_out), .in_0(CNT[0]), .in_1(d_ff_5_nq), .out(multiplexer_1_out));
  Multiplexer #(.Selector_Bits(2)) multiplexer_2 (
    .sel(decoder_1_out_6), .in_0(multiplexer_1_out), .in_1(decoder_1_out_0), .in_2(decoder_1_out_15),
    .in_3(decoder_1_out_15), .out(multiplexer_2_out));
  Multiplexer multiplexer_3 (.sel(and_3_out), .in_0(CNT[1]), .in_1(d_ff_6_nq), .out(multiplexer_3_out));
  Multiplexer multiplexer_4 (.sel(and_4_out), .in_0(CNT[2]), .in_1(d_ff_7_nq), .out(multiplexer_4_out));
  Multiplexer multiplexer_5 (.sel(and_5_out), .in_0(CNT[3]), .in_1(d_ff_8_nq), .out(multiplexer_5_out));
  Multiplexer #(.Selector_Bits(2)) multiplexer_6 (
    .sel(decoder_1_out_6), .in_0(multiplexer_3_out), .in_1(decoder_1_out_15), .in_2(decoder_1_out_15),
    .in_3(decoder_1_out_15), .out(multiplexer_6_out));
  Multiplexer #(.Selector_Bits(2)) multiplexer_7 (
    .sel(decoder_1_out_6), .in_0(multiplexer_4_out), .in_1(decoder_1_out_0), .in_2(decoder_1_out_15),
    .in_3(decoder_1_out_15), .out(multiplexer_7_out));
  Multiplexer #(.Selector_Bits(2)) multiplexer_8 (
    .sel(decoder_1_out_6), .in_0(multiplexer_5_out), .in_1(decoder_1_out_15), .in_2(decoder_1_out_15),
    .in_3(decoder_1_out_15), .out(multiplexer_8_out));
  and and_6 (decoder_1_out_6[0], and_1_out, decoder_1_out_0);
  D_FF d_ff_5 (.D(multiplexer_2_out), .C(CLK), .Q(CNT[0]), .nQ(d_ff_5_nq));
  Multiplexer multiplexer_9 (.sel(and_2_out), .in_0(d_ff_5_nq), .in_1(CNT[0]), .out(multiplexer_9_out));
  D_FF d_ff_6 (.D(multiplexer_6_out), .C(CLK), .Q(CNT[1]), .nQ(d_ff_6_nq));
  Multiplexer multiplexer_10 (.sel(and_2_out), .in_0(d_ff_6_nq), .in_1(CNT[1]), .out(multiplexer_10_out));
  D_FF d_ff_7 (.D(multiplexer_7_out), .C(CLK), .Q(CNT[2]), .nQ(d_ff_7_nq));
  Multiplexer multiplexer_11 (.sel(and_2_out), .in_0(d_ff_7_nq), .in_1(CNT[2]), .out(multiplexer_11_out));
  D_FF d_ff_8 (.D(multiplexer_8_out), .C(CLK), .Q(CNT[3]), .nQ(d_ff_8_nq));
  Decoder #(.Selector_Bits(4)) decoder_1 (
    .sel(CNT), .out_0(decoder_1_out_0), .out_6(decoder_1_out_6[1]), .out_15(decoder_1_out_15));  // open: out_1, out_2, out_3, out_4, out_5, out_7, out_8, out_9, out_10, out_11, out_12, out_13, out_14
endmodule
