// Digital circuit labtimer.dig as structural Verilog
module labtimer (
  input  clk,
  input  SW,
  input  B3,
  input  B2,
  input  B1,
  input  B0,
  input  hz1,
  output [3:0] M10,
  output [3:0] M1,
  output [3:0] S10,
  output [3:0] S1
);

  wire and_1_out, and_2_out, and_3_out, and_4_out, and_5_out, and_6_out, and_7_out, and_8_out, and_9_out,
       and_10_out, and_11_out, and_12_out, and_13_out, d_ff_1_q, d_ff_2_q, d_ff_3_q, d_ff_4_q, d_ff_5_q,
       d_ff_6_q, d_ff_7_q, d_ff_8_q, d_ff_9_q, d_reset_1_q, d_reset_1_q_2, decoder_1_out_0, decoder_1_out_9,
       decoder_2_out_0, decoder_2_out_9, decoder_3_out_0, decoder_3_out_5, multiplexer_1_out,
       multiplexer_2_out, multiplexer_3_out, multiplexer_4_out, not_1_out, not_2_out, not_3_out, not_4_out,
       not_5_out, or_1_out;
  wire [3:0] nor_1_out;

  and and_1 (and_1_out, decoder_2_out_9, and_2_out);
  and and_2 (and_2_out, decoder_3_out_5, decoder_1_out_9);
  D_FF d_ff_1 (.D(and_1_out), .C(hz1), .Q(d_ff_1_q));  // open: nQ
  D_FF d_ff_2 (.D(and_2_out), .C(hz1), .Q(d_ff_2_q));  // open: nQ
  not not_1 (not_1_out, B1);
  D_FF d_ff_3 (.D(decoder_1_out_9), .C(hz1), .Q(d_ff_3_q));  // open: nQ
  not not_2 (not_2_out, B2);
  not not_3 (not_3_out, B3);
  and and_3 (and_3_out, SW, not_2_out);
  not not_4 (not_4_out, B0);
  and and_4 (and_4_out, not_5_out, d_reset_1_q);
  and and_5 (and_5_out, SW, not_3_out);
  and and_6 (and_6_out, SW, not_1_out);
  and and_7 (and_7_out, SW, not_4_out);
  not not_5 (not_5_out, SW);
  Multiplexer multiplexer_1 (.sel(and_4_out), .in_0(and_5_out), .in_1(d_ff_1_q), .out(multiplexer_1_out));
  Multiplexer multiplexer_2 (.sel(and_4_out), .in_0(and_3_out), .in_1(d_ff_2_q), .out(multiplexer_2_out));
  Multiplexer multiplexer_3 (.sel(and_4_out), .in_0(and_6_out), .in_1(d_ff_3_q), .out(multiplexer_3_out));
  Multiplexer multiplexer_4 (.sel(and_4_out), .in_0(and_7_out), .in_1(hz1), .out(multiplexer_4_out));
  and and_8 (and_8_out, hz1, d_reset_1_q_2, not_5_out);
  counter_10 counter_10_1 (.UP(multiplexer_1_out), .DOWN(and_10_out), .CLK(clk), .CNT(M10));
  counter_10 counter_10_2 (.UP(multiplexer_2_out), .DOWN(and_11_out), .CLK(clk), .CNT(M1));
  counter_6 counter_6_1 (.UP(multiplexer_3_out), .DOWN(and_9_out), .CLK(clk), .CNT(S10));
  counter_10 counter_10_3 (.UP(multiplexer_4_out), .DOWN(and_8_out), .CLK(clk), .CNT(S1));
  and and_9 (and_9_out, d_reset_1_q_2, not_5_out, d_ff_4_q);
  and and_10 (and_10_out, not_5_out, d_ff_6_q, d_reset_1_q_2, d_ff_8_q, d_ff_4_q);
  D_FF d_ff_4 (.D(d_ff_5_q), .C(clk), .Q(d_ff_4_q));  // open: nQ
  D_FF d_ff_5 (.D(and_12_out), .C(hz1), .Q(d_ff_5_q));  // open: nQ
  and and_11 (and_11_out, d_ff_4_q, d_ff_8_q, d_reset_1_q_2, not_5_out);
  D_FF d_ff_6 (.D(d_ff_7_q), .C(clk), .Q(d_ff_6_q));  // open: nQ
  and and_12 (and_12_out, decoder_1_out_0, d_reset_1_q_2);
  Decoder #(.Selector_Bits(4)) decoder_1 (
    .sel(S1), .out_0(decoder_1_out_0), .out_9(decoder_1_out_9));  // open: out_1, out_2, out_3, out_4, out_5, out_6, out_7, out_8, out_10, out_11, out_12, out_13, out_14, out_15
  D_FF d_ff_7 (.D(decoder_2_out_0), .C(hz1), .Q(d_ff_7_q));  // open: nQ
  D_FF d_ff_8 (.D(d_ff_9_q), .C(clk), .Q(d_ff_8_q));  // open: nQ
  Decoder #(.Selector_Bits(4)) decoder_2 (
    .sel(M1), .out_0(decoder_2_out_0), .out_9(decoder_2_out_9));  // open: out_1, out_2, out_3, out_4, out_5, out_6, out_7, out_8, out_10, out_11, out_12, out_13, out_14, out_15
  D_FF d_ff_9 (.D(decoder_3_out_0), .C(hz1), .Q(d_ff_9_q));  // open: nQ
  Decoder #(.Selector_Bits(4)) decoder_3 (
    .sel(S10), .out_0(decoder_3_out_0), .out_5(decoder_3_out_5));  // open: out_1, out_2, out_3, out_4, out_6, out_7, out_8, out_9, out_10, out_11, out_12, out_13, out_14, out_15
  assign nor_1_out = ~(S1 | S10 | M1 | M10);  // NOr nor_1, 4 bits wide
  and and_13 (and_13_out, nor_1_out[0], nor_1_out[1], nor_1_out[2], nor_1_out[3]);
  or or_1 (or_1_out, d_reset_1_q, and_13_out);
  D_reset d_reset_1 (.CLK(clk), .D(or_1_out), .RST(SW), .Q(d_reset_1_q), .Q_2(d_reset_1_q_2));

  // Notes on the sheet:
  //   clk: default 1
  //   SW: default 1
  //   B3: default 1
  //   B2: default 1
  //   B1: default 1
  //   B0: default 1
  //   hz1: default 1
endmodule
