// Digital circuit testbench.dig as structural Verilog
module testbench (
  input  clk
);

  wire button_1_out, button_2_out, button_3_out, button_4_out, dipswitch_1_out, u_clkdiv10_hz10;
  wire [3:0] labtimer_1_m1, labtimer_1_m10, labtimer_1_s1, labtimer_1_s10;

  clkdiv10 #(.applicationType("IVERILOG")) u_clkdiv10 (.clk(clk), .sw(dipswitch_1_out), .hz10(u_clkdiv10_hz10));
  DipSwitch #(.dipDefault("true")) dipswitch_1 (.out(dipswitch_1_out));
  Button #(.activeLow("true")) button_1 (.out(button_1_out));
  Button #(.activeLow("true")) button_2 (.out(button_2_out));
  Button #(.activeLow("true")) button_3 (.out(button_3_out));
  Button #(.activeLow("true")) button_4 (.out(button_4_out));
  labtimer labtimer_1 (
    .clk(clk), .SW(dipswitch_1_out), .B3(button_1_out), .B2(button_2_out), .B1(button_3_out),
    .B0(button_4_out), .hz1(u_clkdiv10_hz10), .M10(labtimer_1_m10), .M1(labtimer_1_m1), .S10(labtimer_1_s10),
    .S1(labtimer_1_s1));
  Seven_Seg_Hex seven_seg_hex_1 (.d(labtimer_1_m10), .dp(1'b0));
  Seven_Seg_Hex seven_seg_hex_2 (.d(labtimer_1_m1), .dp(1'b0));
  Seven_Seg_Hex seven_seg_hex_3 (.d(labtimer_1_s10), .dp(1'b0));
  Seven_Seg_Hex seven_seg_hex_4 (.d(labtimer_1_s1), .dp(1'b0));

  // Notes on the sheet:
  //   clk: Hz: 100
  //   SET
  //   RUN
  //   M10
  //   M1
  //   S10
  //   S1
endmodule

/* Code of clkdiv10:
module clkdiv10(
  input  wire clk,    // 100 Hz örneği
  input  wire sw,     // reset
  output wire hz10    // 10 Hz çıkış
);
  // 0…9 saymak için 4 bit yeterli
  reg [3:0] cnt;

  // cnt 9 olduğunda darbe üret
  assign hz10 = (cnt == 4'd9);

  always @(posedge clk) begin
    if (sw)
      cnt <= 4'd0;       
    else
      cnt <= cnt + 4'd1;  
  end
endmodule
*/
